// Logisim project corg-final.circ as structural Verilog: 4 circuits, main circuit main
module main (
  output [15:0] out_1
);

  wire ADD, and_1_out, and_2_out, and_3_out, and_4_out, and_5_out, and_6_out, and_7_out, and_8_out,
       and_9_out, and_10_out, and_11_out, and_12_out, and_13_out, and_14_out, and_15_out, and_16_out,
       and_17_out, and_18_out, and_19_out, and_20_out, and_21_out, and_22_out, and_23_out, and_24_out,
       and_25_out, and_26_out, and_27_out, and_28_out, and_29_out, and_30_out, and_31_out, and_32_out,
       clock_1_out, DEC, decoder_1_out0, decoder_1_out5, decoder_8_out0, decoder_8_out2, decoder_8_out3,
       decoder_9_out0, decoder_9_out1, decoder_10_out0, decoder_10_out1, decoder_11_out0, decoder_11_out1,
       decoder_12_out0, decoder_12_out1, decoder_13_out0, decoder_13_out1, decoder_14_out0, decoder_14_out1,
       decoder_15_out0, decoder_15_out1, decoder_16_out0, decoder_16_out5, decoder_16_out6, decoder_16_out7,
       decoder_23_out0, decoder_23_out1, decoder_24_out0, decoder_24_out1, decoder_25_out0, decoder_25_out1,
       decoder_27_out0, decoder_27_out1, decoder_28_out0, decoder_28_out1, decoder_29_out0, decoder_29_out1,
       decoder_30_out0, decoder_30_out1, INC, IR_EN, IR_LH, IRTODST, LSSRC, MARTIRH, MARTIRL, MEM_CLR,
       MEM_LD, MEM_SEL, MEM_STR, MTDST, MuxCSel, NOT, not_1_out, not_2_out, not_3_out, not_4_out, not_5_out,
       not_6_out, not_7_out, not_8_out, not_9_out, not_10_out, not_11_out, not_12_out, not_13_out,
       not_14_out, not_15_out, not_16_out, not_17_out, not_18_out, not_19_out, not_20_out, not_21_out,
       not_22_out, not_23_out, not_24_out, not_25_out, or_6_out, RSSRC, SPTSRC, SRCTDST, SRCTOM, SRCTSP,
       tunnel;
  wire [1:0] _3RB_FS, _4RB_FS, controlled_buffer_10_out, controlled_buffer_23_out, controlled_buffer_32_out,
       controlled_buffer_38_out, controlled_buffer_44_out, controlled_buffer_61_out,
       controlled_buffer_65_out, controlled_buffer_70_out, controlled_buffer_73_out,
       controlled_buffer_74_out, controlled_buffer_76_out, controlled_buffer_80_out,
       controlled_buffer_86_out, controlled_buffer_92_out, controlled_buffer_97_out,
       controlled_buffer_104_out, controlled_buffer_123_out, controlled_buffer_131_out,
       controlled_buffer_132_out, controlled_buffer_137_out, controlled_buffer_138_out,
       controlled_buffer_143_out, controlled_buffer_144_out, controlled_buffer_149_out,
       controlled_buffer_152_out, controlled_buffer_154_out, controlled_buffer_155_out,
       controlled_buffer_159_out, controlled_buffer_160_out, controlled_buffer_163_out,
       controlled_buffer_175_out, controlled_buffer_176_out, controlled_buffer_177_out,
       controlled_buffer_182_out, controlled_buffer_183_out, controlled_buffer_188_out,
       controlled_buffer_189_out, controlled_buffer_194_out, controlled_buffer_197_out,
       controlled_buffer_210_out, controlled_buffer_211_out, IR_FS, MuxASel, MuxBSel, OutASel, OutBSel,
       outcdecoder_4_out_2, outcdecoder_5_out_2, outcdecoder_14_out_2, outcdecoder_15_out_2, OutCSel, OutDSel;
  wire [2:0] F1, F2, F3;
  wire [3:0] _3RB_RS, _4RB_RS, ALUFlags, ALUFS;

  assign OutDSel = SRCTSP ? 2'b10 : 2'bz;  // Controlled_Buffer controlled_buffer_1
  assign MEM_SEL = SRCTSP ? 1'b1 : 1'bz;  // Controlled_Buffer controlled_buffer_2
  assign MEM_LD = SRCTSP ? 1'b1 : 1'bz;  // Controlled_Buffer controlled_buffer_3
  assign MEM_STR = SRCTSP ? 1'b1 : 1'bz;  // Controlled_Buffer controlled_buffer_4
  assign MEM_CLR = SRCTSP ? 1'b0 : 1'bz;  // Controlled_Buffer controlled_buffer_5
  Decoder #(.select(3), .enable("false")) decoder_1 (
    .out0(decoder_1_out0), .out1(SRCTDST), .out2(MTDST), .out3(IRTODST), .out4(INC), .out5(decoder_1_out5),
    .out6(DEC), .out7(SRCTOM), .sel(F1));
  not not_1 (not_1_out, out_1[10]);
  and and_1 (and_1_out, SRCTDST, not_1_out, not_6_out);
  assign OutASel = and_1_out ? out_1[6:5] : 2'bz;  // Controlled_Buffer controlled_buffer_6
  assign MuxCSel = and_1_out ? 1'b1 : 1'bz;  // Controlled_Buffer controlled_buffer_7
  assign ALUFS = and_1_out ? 4'b0000 : 4'bz;  // Controlled_Buffer controlled_buffer_8
  assign MuxASel = and_1_out ? 2'b11 : 2'bz;  // Controlled_Buffer controlled_buffer_9
  Decoder #(.select(2)) decoder_2 (
    .out0(_4RB_RS[0]), .out1(_4RB_RS[1]), .out2(_4RB_RS[2]), .out3(_4RB_RS[3]),
    .sel(controlled_buffer_10_out), .en(and_1_out));
  assign controlled_buffer_10_out = and_1_out ? out_1[9:8] : 2'bz;  // Controlled_Buffer controlled_buffer_10
  assign _4RB_FS = and_1_out ? 2'b01 : 2'bz;  // Controlled_Buffer controlled_buffer_11
  assign IR_EN = MARTIRL ? 1'b1 : 1'bz;  // Controlled_Buffer controlled_buffer_12
  assign MEM_SEL = MARTIRL ? 1'b1 : 1'bz;  // Controlled_Buffer controlled_buffer_13
  assign MEM_LD = MARTIRL ? 1'b1 : 1'bz;  // Controlled_Buffer controlled_buffer_14
  assign IR_FS = MARTIRL ? 2'b11 : 2'bz;  // Controlled_Buffer controlled_buffer_15
  assign IR_LH = MARTIRL ? 1'b0 : 1'bz;  // Controlled_Buffer controlled_buffer_16
  assign OutDSel = MARTIRL ? 2'b00 : 2'bz;  // Controlled_Buffer controlled_buffer_17
  assign _3RB_FS = MARTIRL ? 2'b10 : 2'bz;  // Controlled_Buffer controlled_buffer_18
  assign _3RB_RS = MARTIRL ? 4'b0001 : 4'bz;  // Controlled_Buffer controlled_buffer_19
  assign MEM_STR = MARTIRL ? 1'b0 : 1'bz;  // Controlled_Buffer controlled_buffer_20
  assign MEM_CLR = MARTIRL ? 1'b0 : 1'bz;  // Controlled_Buffer controlled_buffer_21
  not not_2 (not_2_out, out_1[10]);
  and and_2 (and_2_out, INC, not_2_out);
  assign _4RB_FS = and_2_out ? 2'b10 : 2'bz;  // Controlled_Buffer controlled_buffer_22
  assign controlled_buffer_23_out = and_2_out ? out_1[9:8] : 2'bz;  // Controlled_Buffer controlled_buffer_23
  assign OutASel = and_2_out ? out_1[9:8] : 2'bz;  // Controlled_Buffer controlled_buffer_24
  assign MuxCSel = and_2_out ? 1'b1 : 1'bz;  // Controlled_Buffer controlled_buffer_25
  assign OutDSel = MTDST ? 2'b01 : 2'bz;  // Controlled_Buffer controlled_buffer_26
  assign MEM_SEL = MTDST ? 1'b1 : 1'bz;  // Controlled_Buffer controlled_buffer_27
  assign MEM_LD = MTDST ? 1'b1 : 1'bz;  // Controlled_Buffer controlled_buffer_28
  assign MEM_STR = MTDST ? 1'b0 : 1'bz;  // Controlled_Buffer controlled_buffer_29
  assign MEM_CLR = MTDST ? 1'b0 : 1'bz;  // Controlled_Buffer controlled_buffer_30
  not not_3 (not_3_out, out_1[7]);
  and and_3 (and_3_out, NOT, not_3_out, not_7_out);
  assign OutASel = and_3_out ? out_1[6:5] : 2'bz;  // Controlled_Buffer controlled_buffer_31
  assign controlled_buffer_32_out = and_3_out ? out_1[9:8] : 2'bz;  // Controlled_Buffer controlled_buffer_32
  assign MuxCSel = and_3_out ? 1'b1 : 1'bz;  // Controlled_Buffer controlled_buffer_33
  assign ALUFS = and_3_out ? 4'b0010 : 4'bz;  // Controlled_Buffer controlled_buffer_34
  assign MuxASel = and_3_out ? 2'b11 : 2'bz;  // Controlled_Buffer controlled_buffer_35
  assign _4RB_FS = and_3_out ? 2'b01 : 2'bz;  // Controlled_Buffer controlled_buffer_36
  not not_4 (not_4_out, out_1[7]);
  and and_4 (and_4_out, LSSRC, not_4_out, not_8_out);
  assign OutASel = and_4_out ? out_1[6:5] : 2'bz;  // Controlled_Buffer controlled_buffer_37
  assign controlled_buffer_38_out = and_4_out ? out_1[9:8] : 2'bz;  // Controlled_Buffer controlled_buffer_38
  assign MuxCSel = and_4_out ? 1'b1 : 1'bz;  // Controlled_Buffer controlled_buffer_39
  assign ALUFS = and_4_out ? 4'b1010 : 4'bz;  // Controlled_Buffer controlled_buffer_40
  assign MuxASel = and_4_out ? 2'b11 : 2'bz;  // Controlled_Buffer controlled_buffer_41
  assign _4RB_FS = and_4_out ? 2'b01 : 2'bz;  // Controlled_Buffer controlled_buffer_42
  not not_5 (not_5_out, out_1[7]);
  and and_5 (and_5_out, RSSRC, not_5_out, not_9_out);
  assign OutASel = and_5_out ? out_1[6:5] : 2'bz;  // Controlled_Buffer controlled_buffer_43
  assign controlled_buffer_44_out = and_5_out ? out_1[9:8] : 2'bz;  // Controlled_Buffer controlled_buffer_44
  assign MuxCSel = and_5_out ? 1'b1 : 1'bz;  // Controlled_Buffer controlled_buffer_45
  assign ALUFS = and_5_out ? 4'b1011 : 4'bz;  // Controlled_Buffer controlled_buffer_46
  assign MuxASel = and_5_out ? 2'b11 : 2'bz;  // Controlled_Buffer controlled_buffer_47
  assign _4RB_FS = and_5_out ? 2'b01 : 2'bz;  // Controlled_Buffer controlled_buffer_48
  Clock clock_1 (.out(clock_1_out));
  CONTROL_UNIT control_unit_1 (
    .in_2(out_1[8]), .NEGATIVE_FLAG(ALUFlags[2]), .ZERO_FLAG(ALUFlags[3]), .OPCODE(out_1[15:11]), .F1(F1),
    .F3(F3), .in_1(clock_1_out), .F2(F2));
  not not_6 (not_6_out, out_1[7]);
  Decoder #(.select(2)) decoder_3 (
    .out0(_4RB_RS[0]), .out1(_4RB_RS[1]), .out2(_4RB_RS[2]), .out3(_4RB_RS[3]),
    .sel(controlled_buffer_23_out), .en(and_2_out));
  and and_6 (and_6_out, SRCTSP, not_10_out);
  not not_7 (not_7_out, out_1[10]);
  Decoder #(.select(2)) decoder_4 (
    .out0(_4RB_RS[0]), .out1(_4RB_RS[1]), .out2(_4RB_RS[2]), .out3(_4RB_RS[3]),
    .sel(controlled_buffer_32_out), .en(and_3_out));
  not not_8 (not_8_out, out_1[10]);
  Decoder #(.select(2)) decoder_5 (
    .out0(_4RB_RS[0]), .out1(_4RB_RS[1]), .out2(_4RB_RS[2]), .out3(_4RB_RS[3]),
    .sel(controlled_buffer_38_out), .en(and_4_out));
  not not_9 (not_9_out, out_1[10]);
  Decoder #(.select(2)) decoder_6 (
    .out0(_4RB_RS[0]), .out1(_4RB_RS[1]), .out2(_4RB_RS[2]), .out3(_4RB_RS[3]),
    .sel(controlled_buffer_44_out), .en(and_5_out));
  assign IR_EN = MARTIRH ? 1'b1 : 1'bz;  // Controlled_Buffer controlled_buffer_49
  assign MEM_SEL = MARTIRH ? 1'b1 : 1'bz;  // Controlled_Buffer controlled_buffer_50
  assign MEM_LD = MARTIRH ? 1'b1 : 1'bz;  // Controlled_Buffer controlled_buffer_51
  assign IR_FS = MARTIRH ? 2'b11 : 2'bz;  // Controlled_Buffer controlled_buffer_52
  assign IR_LH = MARTIRH ? 1'b1 : 1'bz;  // Controlled_Buffer controlled_buffer_53
  assign OutDSel = MARTIRH ? 2'b00 : 2'bz;  // Controlled_Buffer controlled_buffer_54
  assign _3RB_FS = MARTIRH ? 2'b10 : 2'bz;  // Controlled_Buffer controlled_buffer_55
  assign _3RB_RS = MARTIRH ? 4'b0001 : 4'bz;  // Controlled_Buffer controlled_buffer_56
  assign MEM_STR = MARTIRH ? 1'b0 : 1'bz;  // Controlled_Buffer controlled_buffer_57
  assign MEM_CLR = MARTIRH ? 1'b0 : 1'bz;  // Controlled_Buffer controlled_buffer_58
  assign MuxASel = MTDST ? 2'b01 : 2'bz;  // Controlled_Buffer controlled_buffer_59
  assign _4RB_FS = MTDST ? 2'b01 : 2'bz;  // Controlled_Buffer controlled_buffer_60
  assign controlled_buffer_61_out = MTDST ? out_1[10:9] : 2'bz;  // Controlled_Buffer controlled_buffer_61
  not not_10 (not_10_out, out_1[10]);
  assign OutASel = and_6_out ? out_1[9:8] : 2'bz;  // Controlled_Buffer controlled_buffer_62
  assign MuxCSel = and_6_out ? 1'b1 : 1'bz;  // Controlled_Buffer controlled_buffer_63
  assign ALUFS = and_6_out ? 4'b0000 : 4'bz;  // Controlled_Buffer controlled_buffer_64
  and and_7 (and_7_out, ADD, out_1[10]);
  and and_8 (and_8_out, SRCTDST, out_1[10], out_1[7]);
  assign controlled_buffer_65_out = and_8_out ? out_1[6:5] : 2'bz;  // Controlled_Buffer controlled_buffer_65
  assign MuxASel = and_8_out ? 2'b10 : 2'bz;  // Controlled_Buffer controlled_buffer_66
  assign MuxCSel = and_8_out ? 1'b0 : 1'bz;  // Controlled_Buffer controlled_buffer_67
  assign ALUFS = and_8_out ? 4'b0000 : 4'bz;  // Controlled_Buffer controlled_buffer_68
  assign MuxBSel = and_8_out ? 2'b11 : 2'bz;  // Controlled_Buffer controlled_buffer_69
  assign controlled_buffer_70_out = and_8_out ? out_1[9:8] : 2'bz;  // Controlled_Buffer controlled_buffer_70
  assign _3RB_FS = and_8_out ? 2'b01 : 2'bz;  // Controlled_Buffer controlled_buffer_71
  Decoder #(.select(2)) decoder_7 (
    .out0(_4RB_RS[0]), .out1(_4RB_RS[1]), .out2(_4RB_RS[2]), .out3(_4RB_RS[3]),
    .sel(controlled_buffer_61_out), .en(MTDST));
  not not_11 (not_11_out, out_1[7]);
  and and_9 (and_9_out, NOT, not_11_out, out_1[10]);
  not not_12 (not_12_out, out_1[7]);
  and and_10 (and_10_out, LSSRC, not_12_out, out_1[10]);
  and and_11 (and_11_out, and_7_out, out_1[7]);
  and and_12 (and_12_out, and_7_out, out_1[4]);
  Decoder #(.select(3), .enable("false")) decoder_8 (
    .out0(decoder_8_out0), .out1(ADD), .out2(decoder_8_out2), .out3(decoder_8_out3), .out4(NOT),
    .out5(LSSRC), .out6(RSSRC), .out7(tunnel), .sel(F2));
  outcdecoder outcdecoder_1 (.in_1(controlled_buffer_65_out), .out_2(OutCSel));
  Decoder #(.select(2), .disabled(0)) decoder_9 (
    .out0(decoder_9_out0), .out1(decoder_9_out1), .out2(_3RB_RS[1]), .out3(_3RB_RS[2]),
    .sel(controlled_buffer_70_out), .en(and_8_out));
  or or_1 (_3RB_RS[0], decoder_9_out0, decoder_9_out1);
  and and_13 (and_13_out, INC, out_1[10]);
  assign _3RB_FS = and_13_out ? 2'b10 : 2'bz;  // Controlled_Buffer controlled_buffer_72
  assign controlled_buffer_73_out = and_13_out ? out_1[9:8] : 2'bz;  // Controlled_Buffer controlled_buffer_73
  Decoder #(.select(2), .disabled(0)) decoder_10 (
    .out0(decoder_10_out0), .out1(decoder_10_out1), .out2(_3RB_RS[1]), .out3(_3RB_RS[2]),
    .sel(controlled_buffer_73_out), .en(and_13_out));
  or or_2 (_3RB_RS[0], decoder_10_out0, decoder_10_out1);
  outcdecoder outcdecoder_2 (.in_1(controlled_buffer_74_out), .out_2(OutCSel));
  assign controlled_buffer_74_out = and_13_out ? out_1[9:8] : 2'bz;  // Controlled_Buffer controlled_buffer_74
  assign MuxCSel = and_13_out ? 1'b0 : 1'bz;  // Controlled_Buffer controlled_buffer_75
  and and_14 (and_14_out, SRCTSP, out_1[10]);
  assign controlled_buffer_76_out = and_14_out ? out_1[9:8] : 2'bz;  // Controlled_Buffer controlled_buffer_76
  assign MuxCSel = and_14_out ? 1'b0 : 1'bz;  // Controlled_Buffer controlled_buffer_77
  assign ALUFS = and_14_out ? 4'b0000 : 4'bz;  // Controlled_Buffer controlled_buffer_78
  assign OutASel = and_9_out ? out_1[6:5] : 2'bz;  // Controlled_Buffer controlled_buffer_79
  Decoder #(.select(2), .disabled(0)) decoder_11 (
    .out0(decoder_11_out0), .out1(decoder_11_out1), .out2(_3RB_RS[1]), .out3(_3RB_RS[2]),
    .sel(controlled_buffer_80_out), .en(and_9_out));
  assign controlled_buffer_80_out = and_9_out ? out_1[9:8] : 2'bz;  // Controlled_Buffer controlled_buffer_80
  or or_3 (_3RB_RS[0], decoder_11_out0, decoder_11_out1);
  assign MuxCSel = and_9_out ? 1'b1 : 1'bz;  // Controlled_Buffer controlled_buffer_81
  assign ALUFS = and_9_out ? 4'b0010 : 4'bz;  // Controlled_Buffer controlled_buffer_82
  assign MuxBSel = and_9_out ? 2'b11 : 2'bz;  // Controlled_Buffer controlled_buffer_83
  assign _3RB_FS = and_9_out ? 2'b01 : 2'bz;  // Controlled_Buffer controlled_buffer_84
  assign OutASel = and_10_out ? out_1[6:5] : 2'bz;  // Controlled_Buffer controlled_buffer_85
  assign controlled_buffer_86_out = and_10_out ? out_1[9:8] : 2'bz;  // Controlled_Buffer controlled_buffer_86
  Decoder #(.select(2), .disabled(0)) decoder_12 (
    .out0(decoder_12_out0), .out1(decoder_12_out1), .out2(_3RB_RS[1]), .out3(_3RB_RS[2]),
    .sel(controlled_buffer_86_out), .en(and_10_out));
  or or_4 (_3RB_RS[0], decoder_12_out0, decoder_12_out1);
  assign MuxCSel = and_10_out ? 1'b1 : 1'bz;  // Controlled_Buffer controlled_buffer_87
  assign ALUFS = and_10_out ? 4'b1010 : 4'bz;  // Controlled_Buffer controlled_buffer_88
  assign MuxBSel = and_10_out ? 2'b11 : 2'bz;  // Controlled_Buffer controlled_buffer_89
  assign _3RB_FS = and_10_out ? 2'b01 : 2'bz;  // Controlled_Buffer controlled_buffer_90
  not not_13 (not_13_out, out_1[7]);
  and and_15 (and_15_out, RSSRC, not_13_out, out_1[10]);
  assign OutASel = and_15_out ? out_1[6:5] : 2'bz;  // Controlled_Buffer controlled_buffer_91
  assign controlled_buffer_92_out = and_15_out ? out_1[9:8] : 2'bz;  // Controlled_Buffer controlled_buffer_92
  assign MuxCSel = and_15_out ? 1'b1 : 1'bz;  // Controlled_Buffer controlled_buffer_93
  assign ALUFS = and_15_out ? 4'b1011 : 4'bz;  // Controlled_Buffer controlled_buffer_94
  assign MuxBSel = and_15_out ? 2'b11 : 2'bz;  // Controlled_Buffer controlled_buffer_95
  assign _3RB_FS = and_15_out ? 2'b01 : 2'bz;  // Controlled_Buffer controlled_buffer_96
  not not_14 (not_14_out, out_1[7]);
  not not_15 (not_15_out, out_1[4]);
  outcdecoder outcdecoder_3 (.in_1(controlled_buffer_76_out), .out_2(OutCSel));
  Decoder #(.select(2), .disabled(0)) decoder_13 (
    .out0(decoder_13_out0), .out1(decoder_13_out1), .out2(_3RB_RS[1]), .out3(_3RB_RS[2]),
    .sel(controlled_buffer_92_out), .en(and_15_out));
  or or_5 (_3RB_RS[0], decoder_13_out0, decoder_13_out1);
  assign controlled_buffer_97_out = and_11_out ? out_1[9:8] : 2'bz;  // Controlled_Buffer controlled_buffer_97
  assign _3RB_FS = and_11_out ? 2'b01 : 2'bz;  // Controlled_Buffer controlled_buffer_98
  assign MuxBSel = and_11_out ? 2'b11 : 2'bz;  // Controlled_Buffer controlled_buffer_99
  assign ALUFS = and_11_out ? 4'b0100 : 4'bz;  // Controlled_Buffer controlled_buffer_100
  assign OutBSel = and_11_out ? out_1[3:2] : 2'bz;  // Controlled_Buffer controlled_buffer_101
  outcdecoder outcdecoder_4 (.in_1(out_1[6:5]), .out_2(outcdecoder_4_out_2));
  assign OutCSel = and_11_out ? outcdecoder_4_out_2 : 2'bz;  // Controlled_Buffer controlled_buffer_102
  assign MuxCSel = and_11_out ? 1'b0 : 1'bz;  // Controlled_Buffer controlled_buffer_103
  and and_16 (and_16_out, and_7_out, not_14_out, not_15_out);
  assign controlled_buffer_104_out = and_12_out ? out_1[9:8] : 2'bz;  // Controlled_Buffer controlled_buffer_104
  assign _3RB_FS = and_12_out ? 2'b01 : 2'bz;  // Controlled_Buffer controlled_buffer_105
  assign MuxBSel = and_12_out ? 2'b11 : 2'bz;  // Controlled_Buffer controlled_buffer_106
  assign ALUFS = and_12_out ? 4'b0100 : 4'bz;  // Controlled_Buffer controlled_buffer_107
  assign OutBSel = and_12_out ? out_1[6:5] : 2'bz;  // Controlled_Buffer controlled_buffer_108
  assign OutCSel = and_12_out ? outcdecoder_5_out_2 : 2'bz;  // Controlled_Buffer controlled_buffer_109
  outcdecoder outcdecoder_5 (.in_1(out_1[3:2]), .out_2(outcdecoder_5_out_2));
  assign MuxCSel = and_12_out ? 1'b0 : 1'bz;  // Controlled_Buffer controlled_buffer_110
  or or_6 (or_6_out, INC, DEC, NOT, LSSRC, RSSRC);
  assign MEM_SEL = or_6_out ? 1'b0 : 1'bz;  // Controlled_Buffer controlled_buffer_111
  assign MEM_LD = or_6_out ? 1'b0 : 1'bz;  // Controlled_Buffer controlled_buffer_112
  assign MEM_STR = or_6_out ? 1'b0 : 1'bz;  // Controlled_Buffer controlled_buffer_113
  assign MEM_CLR = or_6_out ? 1'b0 : 1'bz;  // Controlled_Buffer controlled_buffer_114
  and and_17 (and_17_out, DEC, not_16_out);
  assign OutBSel = SRCTOM ? out_1[10:9] : 2'bz;  // Controlled_Buffer controlled_buffer_115
  assign ALUFS = SRCTOM ? 4'b0001 : 4'bz;  // Controlled_Buffer controlled_buffer_116
  assign MEM_SEL = SRCTOM ? 1'b1 : 1'bz;  // Controlled_Buffer controlled_buffer_117
  assign MEM_LD = SRCTOM ? 1'b1 : 1'bz;  // Controlled_Buffer controlled_buffer_118
  assign MEM_STR = SRCTOM ? 1'b1 : 1'bz;  // Controlled_Buffer controlled_buffer_119
  assign MEM_CLR = SRCTOM ? 1'b0 : 1'bz;  // Controlled_Buffer controlled_buffer_120
  assign OutDSel = SRCTOM ? 2'b01 : 2'bz;  // Controlled_Buffer controlled_buffer_121
  Decoder #(.select(2), .disabled(0)) decoder_14 (
    .out0(decoder_14_out0), .out1(decoder_14_out1), .out2(_3RB_RS[1]), .out3(_3RB_RS[2]),
    .sel(controlled_buffer_97_out), .en(and_11_out));
  or or_7 (_3RB_RS[0], decoder_14_out0, decoder_14_out1);
  Decoder #(.select(2), .disabled(0)) decoder_15 (
    .out0(decoder_15_out0), .out1(decoder_15_out1), .out2(_3RB_RS[1]), .out3(_3RB_RS[2]),
    .sel(controlled_buffer_104_out), .en(and_12_out));
  or or_8 (_3RB_RS[0], decoder_15_out0, decoder_15_out1);
  part2_edited_main main_1 (
    .OutASel(OutASel), .OutBSel(OutBSel), .FunSel_2(_4RB_FS), .RegSel(_4RB_RS), .MuxASel(MuxASel),
    .OutCSel(OutCSel), .OutDSel(OutDSel), .FunSel_3(_3RB_FS), .RegSel_2(_3RB_RS), .L_H(IR_LH),
    .Enable(IR_EN), .FunSel_4(IR_FS), .MuxCSel(MuxCSel), .MuxBSel(MuxBSel), .FunSel(ALUFS), .in_10(MEM_STR),
    .in_11(MEM_SEL), .in_12(MEM_LD), .in_13(MEM_CLR), .out_22(ALUFlags), .out_23(out_1), .in_2(clock_1_out));  // open: out_21
  Decoder #(.select(3), .enable("false")) decoder_16 (
    .out0(decoder_16_out0), .out1(MARTIRL), .out2(MARTIRH), .out3(SRCTSP), .out4(SPTSRC),
    .out5(decoder_16_out5), .out6(decoder_16_out6), .out7(decoder_16_out7), .sel(F3));
  not not_16 (not_16_out, out_1[10]);
  assign _4RB_FS = and_17_out ? 2'b11 : 2'bz;  // Controlled_Buffer controlled_buffer_122
  Decoder #(.select(2)) decoder_17 (
    .out0(_4RB_RS[0]), .out1(_4RB_RS[1]), .out2(_4RB_RS[2]), .out3(_4RB_RS[3]),
    .sel(controlled_buffer_123_out), .en(and_17_out));
  assign controlled_buffer_123_out = and_17_out ? out_1[9:8] : 2'bz;  // Controlled_Buffer controlled_buffer_123
  assign OutASel = and_17_out ? out_1[9:8] : 2'bz;  // Controlled_Buffer controlled_buffer_124
  assign MuxCSel = and_17_out ? 1'b1 : 1'bz;  // Controlled_Buffer controlled_buffer_125
  assign OutDSel = SPTSRC ? 2'b10 : 2'bz;  // Controlled_Buffer controlled_buffer_126
  assign MEM_SEL = SPTSRC ? 1'b1 : 1'bz;  // Controlled_Buffer controlled_buffer_127
  assign MEM_LD = SPTSRC ? 1'b1 : 1'bz;  // Controlled_Buffer controlled_buffer_128
  assign MEM_STR = SPTSRC ? 1'b0 : 1'bz;  // Controlled_Buffer controlled_buffer_129
  assign MEM_CLR = SPTSRC ? 1'b0 : 1'bz;  // Controlled_Buffer controlled_buffer_130
  and and_18 (and_18_out, NOT, out_1[7], not_18_out);
  outcdecoder outcdecoder_6 (.in_1(controlled_buffer_131_out), .out_2(OutCSel));
  assign controlled_buffer_131_out = and_18_out ? out_1[6:5] : 2'bz;  // Controlled_Buffer controlled_buffer_131
  Decoder #(.select(2)) decoder_18 (
    .out0(_4RB_RS[0]), .out1(_4RB_RS[1]), .out2(_4RB_RS[2]), .out3(_4RB_RS[3]),
    .sel(controlled_buffer_132_out), .en(and_18_out));
  assign controlled_buffer_132_out = and_18_out ? out_1[9:8] : 2'bz;  // Controlled_Buffer controlled_buffer_132
  assign MuxCSel = and_18_out ? 1'b0 : 1'bz;  // Controlled_Buffer controlled_buffer_133
  assign ALUFS = and_18_out ? 4'b0010 : 4'bz;  // Controlled_Buffer controlled_buffer_134
  assign MuxASel = and_18_out ? 2'b11 : 2'bz;  // Controlled_Buffer controlled_buffer_135
  assign _4RB_FS = and_18_out ? 2'b01 : 2'bz;  // Controlled_Buffer controlled_buffer_136
  and and_19 (and_19_out, LSSRC, out_1[7], not_19_out);
  outcdecoder outcdecoder_7 (.in_1(controlled_buffer_137_out), .out_2(OutCSel));
  assign controlled_buffer_137_out = and_19_out ? out_1[6:5] : 2'bz;  // Controlled_Buffer controlled_buffer_137
  Decoder #(.select(2)) decoder_19 (
    .out0(_4RB_RS[0]), .out1(_4RB_RS[1]), .out2(_4RB_RS[2]), .out3(_4RB_RS[3]),
    .sel(controlled_buffer_138_out), .en(and_19_out));
  assign controlled_buffer_138_out = and_19_out ? out_1[9:8] : 2'bz;  // Controlled_Buffer controlled_buffer_138
  assign MuxCSel = and_19_out ? 1'b0 : 1'bz;  // Controlled_Buffer controlled_buffer_139
  assign ALUFS = and_19_out ? 4'b1010 : 4'bz;  // Controlled_Buffer controlled_buffer_140
  assign MuxASel = and_19_out ? 2'b11 : 2'bz;  // Controlled_Buffer controlled_buffer_141
  assign _4RB_FS = and_19_out ? 2'b01 : 2'bz;  // Controlled_Buffer controlled_buffer_142
  and and_20 (and_20_out, RSSRC, out_1[7], not_20_out);
  assign controlled_buffer_143_out = and_20_out ? out_1[6:5] : 2'bz;  // Controlled_Buffer controlled_buffer_143
  Decoder #(.select(2)) decoder_20 (
    .out0(_4RB_RS[0]), .out1(_4RB_RS[1]), .out2(_4RB_RS[2]), .out3(_4RB_RS[3]),
    .sel(controlled_buffer_144_out), .en(and_20_out));
  assign controlled_buffer_144_out = and_20_out ? out_1[9:8] : 2'bz;  // Controlled_Buffer controlled_buffer_144
  assign MuxCSel = and_20_out ? 1'b0 : 1'bz;  // Controlled_Buffer controlled_buffer_145
  assign ALUFS = and_20_out ? 4'b1011 : 4'bz;  // Controlled_Buffer controlled_buffer_146
  assign MuxASel = and_20_out ? 2'b11 : 2'bz;  // Controlled_Buffer controlled_buffer_147
  assign _4RB_FS = and_20_out ? 2'b01 : 2'bz;  // Controlled_Buffer controlled_buffer_148
  not not_17 (not_17_out, out_1[10]);
  and and_21 (and_21_out, SRCTDST, not_17_out, out_1[7]);
  assign controlled_buffer_149_out = and_21_out ? out_1[6:5] : 2'bz;  // Controlled_Buffer controlled_buffer_149
  assign MuxASel = and_21_out ? 2'b10 : 2'bz;  // Controlled_Buffer controlled_buffer_150
  assign _4RB_FS = and_21_out ? 2'b01 : 2'bz;  // Controlled_Buffer controlled_buffer_151
  Decoder #(.select(2)) decoder_21 (
    .out0(_4RB_RS[0]), .out1(_4RB_RS[1]), .out2(_4RB_RS[2]), .out3(_4RB_RS[3]),
    .sel(controlled_buffer_152_out), .en(and_21_out));
  assign controlled_buffer_152_out = and_21_out ? out_1[9:8] : 2'bz;  // Controlled_Buffer controlled_buffer_152
  not not_18 (not_18_out, out_1[10]);
  not not_19 (not_19_out, out_1[10]);
  not not_20 (not_20_out, out_1[10]);
  outcdecoder outcdecoder_8 (.in_1(controlled_buffer_143_out), .out_2(OutCSel));
  Hex_Digit_Display hex_digit_display_1 (.value(out_1[15:12]));  // open: dp
  outcdecoder outcdecoder_9 (.in_1(controlled_buffer_149_out), .out_2(OutCSel));
  and and_22 (and_22_out, SPTSRC, not_21_out);
  Hex_Digit_Display hex_digit_display_2 (.value(out_1[7:4]));  // open: dp
  Hex_Digit_Display hex_digit_display_3 (.value(out_1[11:8]));  // open: dp
  and and_23 (and_23_out, DEC, out_1[10]);
  assign _3RB_FS = and_23_out ? 2'b11 : 2'bz;  // Controlled_Buffer controlled_buffer_153
  assign controlled_buffer_154_out = and_23_out ? out_1[9:8] : 2'bz;  // Controlled_Buffer controlled_buffer_154
  assign controlled_buffer_155_out = and_23_out ? out_1[9:8] : 2'bz;  // Controlled_Buffer controlled_buffer_155
  assign MuxCSel = and_23_out ? 1'b0 : 1'bz;  // Controlled_Buffer controlled_buffer_156
  assign MuxASel = IRTODST ? 2'b00 : 2'bz;  // Controlled_Buffer controlled_buffer_157
  assign _4RB_FS = IRTODST ? 2'b01 : 2'bz;  // Controlled_Buffer controlled_buffer_158
  assign controlled_buffer_159_out = IRTODST ? out_1[10:9] : 2'bz;  // Controlled_Buffer controlled_buffer_159
  not not_21 (not_21_out, out_1[10]);
  Decoder #(.select(2)) decoder_22 (
    .out0(_4RB_RS[0]), .out1(_4RB_RS[1]), .out2(_4RB_RS[2]), .out3(_4RB_RS[3]),
    .sel(controlled_buffer_160_out), .en(and_22_out));
  assign controlled_buffer_160_out = and_22_out ? out_1[9:8] : 2'bz;  // Controlled_Buffer controlled_buffer_160
  assign _4RB_FS = and_22_out ? 2'b01 : 2'bz;  // Controlled_Buffer controlled_buffer_161
  assign MuxASel = and_22_out ? 2'b01 : 2'bz;  // Controlled_Buffer controlled_buffer_162
  Decoder #(.select(2), .disabled(0)) decoder_23 (
    .out0(decoder_23_out0), .out1(decoder_23_out1), .out2(_3RB_RS[1]), .out3(_3RB_RS[2]),
    .sel(controlled_buffer_163_out), .en(and_16_out));
  assign controlled_buffer_163_out = and_16_out ? out_1[9:8] : 2'bz;  // Controlled_Buffer controlled_buffer_163
  or or_9 (_3RB_RS[0], decoder_23_out0, decoder_23_out1);
  assign _3RB_FS = and_16_out ? 2'b01 : 2'bz;  // Controlled_Buffer controlled_buffer_164
  assign MuxBSel = and_16_out ? 2'b11 : 2'bz;  // Controlled_Buffer controlled_buffer_165
  assign ALUFS = and_16_out ? 4'b0100 : 4'bz;  // Controlled_Buffer controlled_buffer_166
  assign OutBSel = and_16_out ? out_1[3:2] : 2'bz;  // Controlled_Buffer controlled_buffer_167
  assign MuxCSel = and_16_out ? 1'b1 : 1'bz;  // Controlled_Buffer controlled_buffer_168
  assign OutASel = and_16_out ? out_1[6:5] : 2'bz;  // Controlled_Buffer controlled_buffer_169
  Hex_Digit_Display hex_digit_display_4 (.value(out_1[3:0]));  // open: dp
  and and_24 (and_24_out, SRCTDST, out_1[10], not_22_out);
  assign OutASel = and_24_out ? out_1[6:5] : 2'bz;  // Controlled_Buffer controlled_buffer_170
  assign MuxCSel = and_24_out ? 1'b1 : 1'bz;  // Controlled_Buffer controlled_buffer_171
  assign ALUFS = and_24_out ? 4'b0000 : 4'bz;  // Controlled_Buffer controlled_buffer_172
  assign MuxBSel = and_24_out ? 2'b11 : 2'bz;  // Controlled_Buffer controlled_buffer_173
  assign _3RB_FS = and_24_out ? 2'b01 : 2'bz;  // Controlled_Buffer controlled_buffer_174
  assign controlled_buffer_175_out = and_24_out ? out_1[9:8] : 2'bz;  // Controlled_Buffer controlled_buffer_175
  Decoder #(.select(2), .disabled(0)) decoder_24 (
    .out0(decoder_24_out0), .out1(decoder_24_out1), .out2(_3RB_RS[1]), .out3(_3RB_RS[2]),
    .sel(controlled_buffer_175_out), .en(and_24_out));
  or or_10 (_3RB_RS[0], decoder_24_out0, decoder_24_out1);
  Decoder #(.select(2), .disabled(0)) decoder_25 (
    .out0(decoder_25_out0), .out1(decoder_25_out1), .out2(_3RB_RS[1]), .out3(_3RB_RS[2]),
    .sel(controlled_buffer_154_out), .en(and_23_out));
  or or_11 (_3RB_RS[0], decoder_25_out0, decoder_25_out1);
  outcdecoder outcdecoder_10 (.in_1(controlled_buffer_155_out), .out_2(OutCSel));
  Decoder #(.select(2)) decoder_26 (
    .out0(_4RB_RS[0]), .out1(_4RB_RS[1]), .out2(_4RB_RS[2]), .out3(_4RB_RS[3]),
    .sel(controlled_buffer_159_out), .en(IRTODST));
  and and_25 (and_25_out, NOT, out_1[7], out_1[10]);
  outcdecoder outcdecoder_11 (.in_1(controlled_buffer_176_out), .out_2(OutCSel));
  assign controlled_buffer_176_out = and_25_out ? out_1[6:5] : 2'bz;  // Controlled_Buffer controlled_buffer_176
  assign controlled_buffer_177_out = and_25_out ? out_1[9:8] : 2'bz;  // Controlled_Buffer controlled_buffer_177
  assign MuxCSel = and_25_out ? 1'b0 : 1'bz;  // Controlled_Buffer controlled_buffer_178
  assign ALUFS = and_25_out ? 4'b0010 : 4'bz;  // Controlled_Buffer controlled_buffer_179
  Controlled_Buffer #(.width(2)) controlled_buffer_180 (.out(MuxBSel), .en(and_25_out));  // open: in
  assign _3RB_FS = and_25_out ? 2'b01 : 2'bz;  // Controlled_Buffer controlled_buffer_181
  and and_26 (and_26_out, LSSRC, out_1[7], out_1[10]);
  assign controlled_buffer_182_out = and_26_out ? out_1[6:5] : 2'bz;  // Controlled_Buffer controlled_buffer_182
  outcdecoder outcdecoder_12 (.in_1(controlled_buffer_182_out), .out_2(OutCSel));
  assign controlled_buffer_183_out = and_26_out ? out_1[9:8] : 2'bz;  // Controlled_Buffer controlled_buffer_183
  assign MuxCSel = and_26_out ? 1'b0 : 1'bz;  // Controlled_Buffer controlled_buffer_184
  assign ALUFS = and_26_out ? 4'b1010 : 4'bz;  // Controlled_Buffer controlled_buffer_185
  assign MuxBSel = and_26_out ? 2'b11 : 2'bz;  // Controlled_Buffer controlled_buffer_186
  assign _3RB_FS = and_26_out ? 2'b01 : 2'bz;  // Controlled_Buffer controlled_buffer_187
  and and_27 (and_27_out, RSSRC, out_1[7], out_1[10]);
  outcdecoder outcdecoder_13 (.in_1(controlled_buffer_188_out), .out_2(OutCSel));
  assign controlled_buffer_188_out = and_27_out ? out_1[6:5] : 2'bz;  // Controlled_Buffer controlled_buffer_188
  assign controlled_buffer_189_out = and_27_out ? out_1[9:8] : 2'bz;  // Controlled_Buffer controlled_buffer_189
  assign MuxCSel = and_27_out ? 1'b0 : 1'bz;  // Controlled_Buffer controlled_buffer_190
  assign ALUFS = and_27_out ? 4'b1011 : 4'bz;  // Controlled_Buffer controlled_buffer_191
  assign MuxBSel = and_27_out ? 2'b11 : 2'bz;  // Controlled_Buffer controlled_buffer_192
  assign _3RB_FS = and_27_out ? 2'b01 : 2'bz;  // Controlled_Buffer controlled_buffer_193
  not not_22 (not_22_out, out_1[7]);
  and and_28 (and_28_out, SPTSRC, out_1[10]);
  Decoder #(.select(2), .disabled(0)) decoder_27 (
    .out0(decoder_27_out0), .out1(decoder_27_out1), .out2(_3RB_RS[1]), .out3(_3RB_RS[2]),
    .sel(controlled_buffer_194_out), .en(and_28_out));
  assign controlled_buffer_194_out = and_28_out ? out_1[9:8] : 2'bz;  // Controlled_Buffer controlled_buffer_194
  or or_12 (_3RB_RS[0], decoder_27_out0, decoder_27_out1);
  assign _3RB_FS = and_28_out ? 2'b01 : 2'bz;  // Controlled_Buffer controlled_buffer_195
  assign MuxBSel = and_28_out ? 2'b10 : 2'bz;  // Controlled_Buffer controlled_buffer_196
  Decoder #(.select(2), .disabled(0)) decoder_28 (
    .out0(decoder_28_out0), .out1(decoder_28_out1), .out2(_3RB_RS[1]), .out3(_3RB_RS[2]),
    .sel(controlled_buffer_177_out), .en(and_25_out));
  or or_13 (_3RB_RS[0], decoder_28_out0, decoder_28_out1);
  Decoder #(.select(2), .disabled(0)) decoder_29 (
    .out0(decoder_29_out0), .out1(decoder_29_out1), .out2(_3RB_RS[1]), .out3(_3RB_RS[2]),
    .sel(controlled_buffer_183_out), .en(and_26_out));
  or or_14 (_3RB_RS[0], decoder_29_out0, decoder_29_out1);
  Decoder #(.select(2), .disabled(0)) decoder_30 (
    .out0(decoder_30_out0), .out1(decoder_30_out1), .out2(_3RB_RS[1]), .out3(_3RB_RS[2]),
    .sel(controlled_buffer_189_out), .en(and_27_out));
  or or_15 (_3RB_RS[0], decoder_30_out0, decoder_30_out1);
  and and_29 (and_29_out, ADD, not_23_out);
  not not_23 (not_23_out, out_1[10]);
  and and_30 (and_30_out, and_29_out, out_1[4]);
  and and_31 (and_31_out, and_29_out, out_1[7]);
  not not_24 (not_24_out, out_1[4]);
  outcdecoder outcdecoder_14 (.in_1(out_1[6:5]), .out_2(outcdecoder_14_out_2));
  and and_32 (and_32_out, and_29_out, not_25_out, not_24_out);
  not not_25 (not_25_out, out_1[7]);
  outcdecoder outcdecoder_15 (.in_1(out_1[3:2]), .out_2(outcdecoder_15_out_2));
  Decoder #(.select(2)) decoder_31 (
    .out0(_4RB_RS[0]), .out1(_4RB_RS[1]), .out2(_4RB_RS[2]), .out3(_4RB_RS[3]),
    .sel(controlled_buffer_197_out), .en(and_31_out));
  assign controlled_buffer_197_out = and_31_out ? out_1[9:8] : 2'bz;  // Controlled_Buffer controlled_buffer_197
  assign _4RB_FS = and_31_out ? 2'b01 : 2'bz;  // Controlled_Buffer controlled_buffer_198
  assign ALUFS = and_31_out ? 4'b0100 : 4'bz;  // Controlled_Buffer controlled_buffer_199
  assign MuxASel = and_31_out ? 2'b11 : 2'bz;  // Controlled_Buffer controlled_buffer_200
  assign OutBSel = and_31_out ? out_1[3:2] : 2'bz;  // Controlled_Buffer controlled_buffer_201
  assign OutCSel = and_31_out ? outcdecoder_14_out_2 : 2'bz;  // Controlled_Buffer controlled_buffer_202
  assign MuxCSel = and_31_out ? 1'b0 : 1'bz;  // Controlled_Buffer controlled_buffer_203
  assign ALUFS = and_30_out ? 4'b0100 : 4'bz;  // Controlled_Buffer controlled_buffer_204
  assign MuxASel = and_30_out ? 2'b11 : 2'bz;  // Controlled_Buffer controlled_buffer_205
  assign OutBSel = and_30_out ? out_1[6:5] : 2'bz;  // Controlled_Buffer controlled_buffer_206
  assign OutCSel = and_30_out ? outcdecoder_15_out_2 : 2'bz;  // Controlled_Buffer controlled_buffer_207
  assign MuxCSel = and_30_out ? 1'b0 : 1'bz;  // Controlled_Buffer controlled_buffer_208
  assign _4RB_FS = and_30_out ? 2'b01 : 2'bz;  // Controlled_Buffer controlled_buffer_209
  assign controlled_buffer_210_out = and_30_out ? out_1[9:8] : 2'bz;  // Controlled_Buffer controlled_buffer_210
  Decoder #(.select(2)) decoder_32 (
    .out0(_4RB_RS[0]), .out1(_4RB_RS[1]), .out2(_4RB_RS[2]), .out3(_4RB_RS[3]),
    .sel(controlled_buffer_210_out), .en(and_30_out));
  assign controlled_buffer_211_out = and_32_out ? out_1[9:8] : 2'bz;  // Controlled_Buffer controlled_buffer_211
  Decoder #(.select(2)) decoder_33 (
    .out0(_4RB_RS[0]), .out1(_4RB_RS[1]), .out2(_4RB_RS[2]), .out3(_4RB_RS[3]),
    .sel(controlled_buffer_211_out), .en(and_32_out));
  assign _4RB_FS = and_32_out ? 2'b01 : 2'bz;  // Controlled_Buffer controlled_buffer_212
  assign MuxASel = and_32_out ? 2'b11 : 2'bz;  // Controlled_Buffer controlled_buffer_213
  assign ALUFS = and_32_out ? 4'b0100 : 4'bz;  // Controlled_Buffer controlled_buffer_214
  assign OutBSel = and_32_out ? out_1[3:2] : 2'bz;  // Controlled_Buffer controlled_buffer_215
  assign MuxCSel = and_32_out ? 1'b1 : 1'bz;  // Controlled_Buffer controlled_buffer_216
  assign OutASel = and_32_out ? out_1[6:5] : 2'bz;  // Controlled_Buffer controlled_buffer_217

  // Other names for the same wires on the sheet: ADDRESS[7:0] = out_1[7:0]; INSTR[15:0] = out_1;
  //   SRCREG2[2:0] = out_1[4:2]; SRCREG1[2:0] = out_1[7:5]; AdrMOD = out_1[8]; DESTREG[2:0] = out_1[10:8];
  //   REGSEL[1:0] = out_1[10:9]; OPCODE[4:0] = out_1[15:11]

  // Notes on the sheet:
  //   MARTIRL
  //   MARTIRH
  //   INC
  //   MTDST
  //   SRCTSP
  //   ADD (DEST IN 3RB)
  //   SRCTODST
  //   NOT
  //   LSSRC
  //   RSSRC
  //   Memory Independent Operations
  //   SRCTOM
  //   DEC
  //   IRTODST
  //   SPTSRC
  //   ADD (DEST IN 4RB)
endmodule

module CONTROL_UNIT (
  input  in_1,
  input  in_2,
  input  NEGATIVE_FLAG,
  input  ZERO_FLAG,
  input  [4:0] OPCODE,
  output [2:0] F1,
  output [2:0] F2,
  output [2:0] F3
);

  wire and_1_out, and_2_out, and_3_out, and_4_out, decoder_1_out0, decoder_1_out1, decoder_1_out2,
       decoder_1_out3, multiplexer_1_out, not_1_out, not_2_out;
  wire [1:0] rom_1_data_3, rom_1_data_4;
  wire [2:0] rom_1_data;
  wire [7:0] adder_1_out, controlled_buffer_1_out, controlled_buffer_4_out, register_1_q, register_2_q,
       rom_1_data_2;
  wire [7:2] adder_2_out;

  not not_1 (not_1_out, multiplexer_1_out);
  and and_1 (and_1_out, decoder_1_out0, not_1_out);
  Adder adder_1 (.a(register_1_q), .b(8'h1), .out(adder_1_out));  // open: cin, cout
  assign controlled_buffer_1_out = and_1_out ? adder_1_out : 8'bz;  // Controlled_Buffer controlled_buffer_1
  and and_2 (and_2_out, decoder_1_out0, multiplexer_1_out);
  assign controlled_buffer_1_out = and_2_out ? rom_1_data_2 : 8'bz;  // Controlled_Buffer controlled_buffer_2
  and and_3 (and_3_out, decoder_1_out1, multiplexer_1_out);
  assign controlled_buffer_1_out = and_3_out ? rom_1_data_2 : 8'bz;  // Controlled_Buffer controlled_buffer_3
  assign controlled_buffer_4_out = and_3_out ? adder_1_out : 8'bz;  // Controlled_Buffer controlled_buffer_4
  not not_2 (not_2_out, multiplexer_1_out);
  and and_4 (and_4_out, decoder_1_out1, not_2_out);
  assign controlled_buffer_1_out = and_4_out ? adder_1_out : 8'bz;  // Controlled_Buffer controlled_buffer_5
  Register register_1 (.D(controlled_buffer_1_out), .Q(register_1_q), .clk(in_1));  // open: en, clr
  Register register_2 (.D(controlled_buffer_4_out), .en(and_3_out), .Q(register_2_q), .clk(in_1));  // open: clr
  assign controlled_buffer_1_out = decoder_1_out3 ? {adder_2_out, 2'b00} : 8'bz;  // Controlled_Buffer controlled_buffer_6
  assign controlled_buffer_1_out = decoder_1_out2 ? register_2_q : 8'bz;  // Controlled_Buffer controlled_buffer_7
  ROM #(.dataWidth(24)) rom_1 (
    .addr(register_1_q), .data({F1, F2, F3, rom_1_data_4, rom_1_data_3, rom_1_data_2, rom_1_data}));  // open: sel
  Decoder #(.select(2), .enable("false")) decoder_1 (
    .out0(decoder_1_out0), .out1(decoder_1_out1), .out2(decoder_1_out2), .out3(decoder_1_out3),
    .sel(rom_1_data_3));
  Multiplexer #(.select(2), .enable("false")) multiplexer_1 (
    .in0(1'b1), .in1(in_2), .in2(NEGATIVE_FLAG), .in3(ZERO_FLAG), .out(multiplexer_1_out), .sel(rom_1_data_4));
  Adder #(.width(5)) adder_2 (.a(OPCODE), .b(5'b00001), .out(adder_2_out[6:2]), .cout(adder_2_out[7]));  // open: cin

  // Notes on the sheet:
  //   Control Unit
  //   CAR
  //   SP
  //   Control Memory
  //   contents of rom_1 (hex, n*v repeats v):
  //   8008 10010 1800 0 402000 600000 0 0 e00000 0 0 0 200000 0 0 0 18088 38000 0 0 300a8 20000 0 0 40000
  //   0 0 0 a00000 0 0 0 200108 c00000 0 0 200128 800000 10*0 100000 0 0 0 140000 0 0 0 180000 0 0 0 28000
  //   0 0 0 6210 0 28000 0 2e000 0 0 0 18248 38250 28000 0 30268 20000
  //   IR LOW PLACEHOLDER
endmodule

module outcdecoder (
  input  [1:0] in_1,
  output [1:0] out_2
);

  Subtractor #(.width(2)) subtractor_1 (.a(in_1), .b(2'b01), .out(out_2));  // open: bin, bout
endmodule

module converter (
  input  [4:0] OPCode,
  input  [1:0] RegSel,
  input  Adressing_Mode,
  input  [7:0] Address,
  input  Type_1,
  input  [4:0] OPCode_2,
  input  [2:0] DestReg,
  input  [2:0] SrcReg1,
  input  [2:0] SrcReg2,
  input  [2:0] F1,
  input  [2:0] F2,
  input  [2:0] F3,
  input  [1:0] CD,
  input  [2:0] FILLER,
  input  [1:0] BR,
  input  [7:0] AD
);

  wire not_1_out;
  wire [15:0] controlled_buffer_1_out;

  assign controlled_buffer_1_out = Type_1 ? {OPCode, RegSel, Adressing_Mode, Address} : 16'bz;  // Controlled_Buffer controlled_buffer_1
  not not_1 (not_1_out, Type_1);
  assign controlled_buffer_1_out = not_1_out ? {OPCode_2, DestReg, SrcReg1, SrcReg2, 2'b00} : 16'bz;  // Controlled_Buffer controlled_buffer_2
  // Probe on controlled_buffer_1_out[7:0]
  // Probe on controlled_buffer_1_out[15:8]
  // Probe on {F1, F2, F3, CD, BR, AD, FILLER}
endmodule
